# Fritzing sketch diagram (saved by Fritzing 0.9.3b)
breadboards: 1

parts:
  LED1 = LED - 5mm [color="Green (565nm)" current=0.030 package="5 mm [THT]"]
  R1 = Resistor [tolerance=±5% resistance=330 power=0.25 package=THT]
  LED2 = LED - 5mm [color="Yellow (585nm)" current=0.030 package="5 mm [THT]"]
  LED3 = LED - 5mm [color="Red (633nm)" current=0.030 package="5 mm [THT]"]
  R2 = Resistor [tolerance=±5% resistance=330 power=0.25 package=THT]
  R3 = Resistor [tolerance=±5% resistance=330 power=0.25 package=THT]
  Mod1 = Raspberry Pi 4B
  J8 = female pin header, 2 pins [form="♀ (female)"]  # not connected
  J9 = female pin header, 2 pins [form="♀ (female)"]
  J7 = female pin header, 2 pins [form="♀ (female)"]  # not connected
  S3 = Square Pushbutton

nets:
  N1: LED1.cathode, R1.Pin_0
  N2: LED1.anode, Mod1.GPIO18
  N3: R1.Pin_1, R2.Pin_1, R3.Pin_1, Mod1.GND, J9.pin1, S3.leg0
  N4: LED2.cathode, R2.Pin_0
  N5: LED2.anode, Mod1.GPIO24
  N6: LED3.cathode, R3.Pin_0
  N7: LED3.anode, Mod1.GPIO25
  N8: Mod1.GPIO5, J9.pin2
  N9: Mod1.GPIO6, S3.leg1

notes:
  Hook switch
  Microphone
  +ve ???
  -ve ???
  Speaker
  +ve (white) -> ???
  -ve (blue) -> ???
  USB Sound Card
  Playback Messages Button
